// Digital circuit GeneralPurposeRegister.dig as structural Verilog
module GeneralPurposeRegister (
  input  clock,
  input  [3:0] \input ,
  input  [1:0] store_clear_load,
  input  [3:0] input1,
  output [3:0] \output 
);

  wire [3:0] add_1_s, multiplexer_1_out;

  Add #(.Bits(4)) add_1 (.a(\output ), .b(input1), .c_i(1'b0), .s(add_1_s));  // open: c_o
  Multiplexer #(.Selector_Bits(2), .Bits(4)) multiplexer_1 (
    .sel(store_clear_load), .in_0(4'b0000), .in_1(\input ), .in_2(\output ), .in_3(add_1_s),
    .out(multiplexer_1_out));
  D_FF d_ff_1 (.D(multiplexer_1_out[3]), .C(clock), .Q(\output [3]));  // open: nQ
  D_FF d_ff_2 (.D(multiplexer_1_out[2]), .C(clock), .Q(\output [2]));  // open: nQ
  D_FF d_ff_3 (.D(multiplexer_1_out[1]), .C(clock), .Q(\output [1]));  // open: nQ
  D_FF d_ff_4 (.D(multiplexer_1_out[0]), .C(clock), .Q(\output [0]));  // open: nQ

  // Notes on the sheet:
  //   store_clear_load: 0 -> clear
  //   1 -> store input
  //   2 -> Load
  //   3 -> Increment
  //   input1: default 1
endmodule
